# Fritzing sketch led_button (saved by Fritzing 0.9.2b)
breadboards: 1

parts:
  LED1 = LED - 3mm [color="Red (633nm)" package="3 mm [THT]"]
  J1 = T Cobbler Plus
  R1 = Resistor [tolerance=±1% resistance=56 package=THT]
  S1 = Momentary Switch [package=tactile-pth]

nets:
  N1: LED1.cathode, R1.Pin_1
  N2: LED1.anode, J1.5.0V
  N3: J1.SCL, R1.Pin_0, S1.4
  N4: J1.#24, S1.2

custom parts:
  T Cobbler Plus: The T-Cobbler Plus is an add on prototyping board from Adafruit specifically designed for the Raspberry Pi B+ that can break out all those tasty power, GPIO, I2C and SPI pins from the 40-pin header onto a solderless breadboard. This set will make "cobbling together" prototypes with the Pi super easy. The T-Cobbler Plus can plug into any solderless breadboard.
