# Fritzing sketch pir (saved by Fritzing 0.9.2b)
breadboards: 2

parts:
  J1 = T Cobbler Plus
  PIR1 = PIR sensor

nets:
  N1: J1.5.0V, PIR1.SIG
  N2: J1.MISO, PIR1.VDD
  N3: J1.SCLK, PIR1.GND

custom parts:
  T Cobbler Plus: The T-Cobbler Plus is an add on prototyping board from Adafruit specifically designed for the Raspberry Pi B+ that can break out all those tasty power, GPIO, I2C and SPI pins from the 40-pin header onto a solderless breadboard. This set will make "cobbling together" prototypes with the Pi super easy. The T-Cobbler Plus can plug into any solderless breadboard.
