# Fritzing sketch pir-led (saved by Fritzing 0.9.2b)
breadboards: 1

parts:
  LED1 = LED - 3mm [color="Red (633nm)" package="3 mm [THT]"]
  PIR1 = PIR sensor
  J1 = T Cobbler Plus
  R2 = Resistor [tolerance=±1% resistance=56 package=THT]

nets:
  N1: LED1.cathode, R2.Pin_1
  N2: LED1.anode, J1.GND
  N3: PIR1.VDD, J1.MISO
  N4: PIR1.SIG, J1.EEC
  N5: PIR1.GND, J1.SCLK
  N6: J1.SCL, R2.Pin_0

custom parts:
  T Cobbler Plus: The T-Cobbler Plus is an add on prototyping board from Adafruit specifically designed for the Raspberry Pi B+ that can break out all those tasty power, GPIO, I2C and SPI pins from the 40-pin header onto a solderless breadboard. This set will make "cobbling together" prototypes with the Pi super easy. The T-Cobbler Plus can plug into any solderless breadboard.
