# Fritzing sketch trafficlights (saved by Fritzing 0.9.2b)
breadboards: 1

parts:
  J1 = T Cobbler Plus
  LED1 = smd LED [color="Red (633nm)" package="0805 [SMD]"]
  LED2 = smd LED [color="Red (633nm)" package="0805 [SMD]"]
  LED3 = smd LED [color="Green (570nm)" package="0805 [SMD]"]
  LED4 = smd LED [color="Yellow (595nm)" package="0805 [SMD]"]
  LED5 = smd LED [color="Green (570nm)" package="0805 [SMD]"]
  S1 = Pushbutton [package="[SMD]"]
  R1 = Resistor [tolerance=±5% resistance=65 package="2010 [SMD]"]
  R2 = Resistor [tolerance=±5% resistance=65 package="2010 [SMD]"]
  R3 = Resistor [tolerance=±5% resistance=65 package="2010 [SMD]"]
  R4 = Resistor [tolerance=±5% resistance=65 package="2010 [SMD]"]
  R5 = Resistor [tolerance=±5% resistance=65 package="2010 [SMD]"]
  LED6 = smd LED [color="Yellow (595nm)" package="0805 [SMD]"]
  R6 = Resistor [tolerance=±5% resistance=65 package="2010 [SMD]"]
  PIR1 = PIR sensor
  R7 = Resistor [tolerance=±5% resistance=6.49k package="2010 [SMD]"]

nets:
  N1: J1.5.0V, S1.Pin_1, S1.Pin_2, R7.Pin_0
  N2: J1.SCL, R1.Pin_0, R2.Pin_0, R3.Pin_0, R7.Pin_1
  N3: J1.#22, LED1.anode
  N4: J1.#23, LED4.anode
  N5: J1.3.3V, LED5.anode
  N6: J1.#24, LED2.anode
  N7: J1.MOSI, LED3.anode
  N8: J1.MISO, PIR1.VDD
  N9: J1.SCLK, R4.Pin_0, R5.Pin_0, R6.Pin_0, PIR1.GND
  N10: LED1.cathode, R1.Pin_1
  N11: LED2.cathode, R4.Pin_1
  N12: LED3.cathode, R5.Pin_1
  N13: LED4.cathode, R2.Pin_1
  N14: LED5.cathode, R3.Pin_1
  N15: LED6.cathode, R6.Pin_1

custom parts:
  T Cobbler Plus: The T-Cobbler Plus is an add on prototyping board from Adafruit specifically designed for the Raspberry Pi B+ that can break out all those tasty power, GPIO, I2C and SPI pins from the 40-pin header onto a solderless breadboard. This set will make "cobbling together" prototypes with the Pi super easy. The T-Cobbler Plus can plug into any solderless breadboard.
